# Fritzing sketch BlinkExternalLed (saved by Fritzing 0.9.2b)
breadboards: 1

parts:
  Onderdeel1 = Arduino Uno (Rev3)
  R1 = Resistor [tolerance=±5% resistance=220 package=THT]
  LED1 = LED - 5mm [color="Red (633nm)" package="5 mm [THT]"]

nets:
  N1: Onderdeel1.D8, R1.Pin_1
  N2: Onderdeel1.GND, LED1.cathode
  N3: R1.Pin_0, LED1.anode

notes:
  [Typ hier uw notitie]
