# Fritzing sketch PingPongLeds (saved by Fritzing 0.9.2b)
breadboards: 1

parts:
  Onderdeel1 = Arduino Uno (Rev3)
  R1 = Resistor [tolerance=±5% resistance=220 package=THT]
  LED1 = LED - 5mm [color="Red (633nm)" package="5 mm [THT]"]
  LED2 = LED - 5mm [color="Green (555nm)" package="5 mm [THT]"]
  R2 = Resistor [tolerance=±5% resistance=220 package=THT]

nets:
  N1: Onderdeel1.D8, R1.Pin_1
  N2: Onderdeel1.GND, LED1.cathode, LED2.cathode
  N3: Onderdeel1.D7, R2.Pin_1
  N4: R1.Pin_0, LED1.anode
  N5: LED2.anode, R2.Pin_0

notes:
  [Typ hier uw notitie]
