# Fritzing sketch LedsMetDrukknop (saved by Fritzing 0.9.2b)
breadboards: 1

parts:
  part = Arduino Uno (Rev3)
  LED1 = LED - 5mm [color="Red (633nm)" package="5 mm [THT]"]
  LED2 = LED - 5mm [color="Green (555nm)" package="5 mm [THT]"]
  R1 = Resistor [tolerance=±5% resistance=220 package=THT]
  R2 = Resistor [tolerance=±5% resistance=220 package=THT]
  S1 = Pushbutton [package="[THT]"]
  R3 = Resistor [tolerance=±5% resistance=10k package=THT]

nets:
  N1: part.D12/MISO, R2.Pin_1
  N2: part.D13/SCK, R1.Pin_1
  N3: part.D2, S1.Pin_1, S1.Pin_2, R3.Pin_0
  N4: part.5V, S1.Pin_3, S1.Pin_4
  N5: part.GND, LED1.cathode, LED2.cathode, R3.Pin_1
  N6: LED1.anode, R1.Pin_0
  N7: LED2.anode, R2.Pin_0
