# Fritzing sketch Spanningsdeler (saved by Fritzing 0.9.2b)
breadboards: 1

parts:
  Onderdeel1 = Arduino Uno (Rev3)
  R1 = Rotary Potentiometer (Small) [maximum_resistance=50kΩ package=THT]
  R2 = Resistor [tolerance=±5% resistance=10k package=THT]

nets:
  N1: Onderdeel1.A0, R1.leg1, R2.Pin_1
  N2: Onderdeel1.GND, R2.Pin_0
  N3: Onderdeel1.5V, R1.wiper
