# Fritzing sketch EenCijfer7SegmentLEDDisplay (saved by Fritzing 0.9.2b)
breadboards: 1

parts:
  Onderdeel1 = Arduino Uno (Rev3)
  U1 = 7-SEGMENT-DISPLAY-1_-RED [package=7-segment-1_pth]
  R1 = Resistor [tolerance=±5% resistance=220 package=THT]

nets:
  N1: Onderdeel1.D8, U1.G
  N2: Onderdeel1.D9_PWM, U1.F
  N3: Onderdeel1.GND, R1.Pin_1
  N4: Onderdeel1.D2, U1.A
  N5: Onderdeel1.D3_PWM, U1.B
  N6: Onderdeel1.D4, U1.C
  N7: Onderdeel1.D5_PWM, U1.DP
  N8: Onderdeel1.D6_PWM, U1.D
  N9: Onderdeel1.D7, U1.E
  N10: U1.G1, U1.G2, R1.Pin_0
