# Fritzing sketch thermometer (saved by Fritzing 0.9.2b)
breadboards: 1

parts:
  T1 = LM35 Temperature Sensor [package="TO92 [THT]"]
  Onderdeel1 = Arduino Uno (Rev3)
  LED1 = 7-SEGMENT-4DIGIT [package=7-segment-4digit]
  R1 = Resistor [tolerance=±5% resistance=220 package=THT]
  R2 = Resistor [tolerance=±5% resistance=220 package=THT]
  R3 = Resistor [tolerance=±5% resistance=220 package=THT]
  R4 = Resistor [tolerance=±5% resistance=220 package=THT]

nets:
  N1: T1.+Vs, Onderdeel1.5V
  N2: T1.Vout, Onderdeel1.A0
  GND: T1.GND, Onderdeel1.GND
  N3: Onderdeel1.D8, LED1.2
  N4: Onderdeel1.D9_PWM, LED1.3
  N5: Onderdeel1.D10_PWM/SS, LED1.4
  N6: Onderdeel1.D11_PWM/MOSI, LED1.5
  N7: Onderdeel1.D12/MISO, R4.Pin_1
  N8: Onderdeel1.D13/SCK, LED1.11
  N9: Onderdeel1.D2, R3.Pin_1
  N10: Onderdeel1.D3_PWM, R2.Pin_1
  N11: Onderdeel1.D4, LED1.14
  N12: Onderdeel1.D5_PWM, LED1.15
  N13: Onderdeel1.D6_PWM, R1.Pin_1
  N14: Onderdeel1.D7, LED1.1
  N15: LED1.6, R4.Pin_0
  N16: LED1.13, R2.Pin_0
  N17: LED1.16, R1.Pin_0
