# Fritzing sketch LedMatrix (saved by Fritzing 0.9.2b)
breadboards: 2

parts:
  Onderdeel1 = Arduino Uno (Rev3)
  Disp1 = 1588BS [part_number=1588BS]
  R1 = Resistor [tolerance=±5% resistance=220 package=THT]
  R2 = Resistor [tolerance=±5% resistance=220 package=THT]
  R3 = Resistor [tolerance=±5% resistance=220 package=THT]
  R4 = Resistor [tolerance=±5% resistance=220 package=THT]
  R5 = Resistor [tolerance=±5% resistance=220 package=THT]
  R6 = Resistor [tolerance=±5% resistance=220 package=THT]
  R7 = Resistor [tolerance=±5% resistance=220 package=THT]
  R8 = Resistor [tolerance=±5% resistance=220 package=THT]

nets:
  N1: Onderdeel1.A0, Disp1.pin_16
  N2: Onderdeel1.A1, Disp1.pin_15
  N3: Onderdeel1.A2, R8.Pin_0
  N4: Onderdeel1.A3, Disp1.pin_13
  N5: Onderdeel1.D8, Disp1.pin_6
  N6: Onderdeel1.D9_PWM, R3.Pin_1
  N7: Onderdeel1.D10_PWM/SS, Disp1.pin_4
  N8: Onderdeel1.D11_PWM/MOSI, Disp1.pin_3
  N9: Onderdeel1.D12/MISO, R2.Pin_1
  N10: Onderdeel1.D13/SCK, R1.Pin_1
  N11: Onderdeel1.D2, R7.Pin_0
  N12: Onderdeel1.D3_PWM, Disp1.pin_11
  N13: Onderdeel1.D4, Disp1.pin_10
  N14: Onderdeel1.D5_PWM, R6.Pin_0
  N15: Onderdeel1.D6_PWM, R5.Pin_1
  N16: Onderdeel1.D7, R4.Pin_1
  N17: Disp1.pin1, R1.Pin_0
  N18: Disp1.pin2, R2.Pin_0
  N19: Disp1.pin_5, R3.Pin_0
  N20: Disp1.pin_7, R4.Pin_0
  N21: Disp1.pin_8, R5.Pin_0
  N22: Disp1.pin_9, R6.Pin_1
  N23: Disp1.pin_12, R7.Pin_1
  N24: Disp1.pin_14, R8.Pin_1

custom parts:
  1588BS: LED Matrix Display 8x8 red 37.5mm
