# Fritzing sketch Infrarood (saved by Fritzing 0.9.2b)
breadboards: 1

parts:
  Onderdeel1 = Arduino Uno (Rev3)
  LED1 = LED - 5mm [color="Red (633nm)" package="5 mm [THT]"]
  LED2 = LED - 5mm [color="Green (570nm)" package="5 mm [THT]"]
  LED3 = LED - 5mm [color="Blue (525nm)" package="5 mm [THT]"]
  R1 = Resistor [tolerance=±5% resistance=220 package=THT]
  R2 = Resistor [tolerance=±5% resistance=220 package=THT]
  R3 = Resistor [tolerance=±5% resistance=220 package=THT]
  U1 = TEMPERATURE-SENSOR [package=to-92]

nets:
  N1: Onderdeel1.D8, R3.Pin_1
  N2: Onderdeel1.D9_PWM, R2.Pin_1
  N3: Onderdeel1.D10_PWM/SS, R1.Pin_1
  N4: Onderdeel1.D2, U1.GND
  5V: Onderdeel1.5V, U1.VCC
  N5: Onderdeel1.GND, LED1.anode, LED2.anode, LED3.anode, U1.ADJ
  N6: LED1.cathode, R1.Pin_0
  N7: LED2.cathode, R2.Pin_0
  N8: LED3.cathode, R3.Pin_0
