# Fritzing sketch LichtsensorGL55xx (saved by Fritzing 0.9.2b)
breadboards: 1

parts:
  PR1 = Photocell (LDR) [package=THT]
  R2 = Rotary Potentiometer (Small) [maximum_resistance=100kΩ package=THT]
  R3 = Resistor [tolerance=±5% resistance=10k package=THT]
  LED1 = LED - 5mm [color="Red (633nm)" package="5 mm [THT]"]
  R1 = Resistor [tolerance=±5% resistance=220 package=THT]
  Onderdeel1 = Arduino Uno (Rev3)

nets:
  N1: PR1.pin_0, R2.wiper
  N2: PR1.pin_1, R3.Pin_0, Onderdeel1.A0
  N3: R2.leg1, R3.Pin_1, LED1.cathode, Onderdeel1.GND
  N4: R2.leg2, Onderdeel1.5V
  N5: LED1.anode, R1.Pin_0
  N6: R1.Pin_1, Onderdeel1.D3_PWM
