# Fritzing sketch MotorSturing (saved by Fritzing 0.9.2b)

parts:
  MA = DC Motor
  S1 = H-Bridge with L298N
  MB = DC Motor
  VCC1 = Battery block 9V
  Onderdeel1 = Arduino Uno (Rev3)

nets:
  N1: MA.pin_1, S1.M1-02
  N2: MA.pin_2, S1.M1-01
  N3: S1.12V, VCC1.+
  GND: S1.GND, VCC1.-, Onderdeel1.GND
  5V: S1.5V, Onderdeel1.5V
  N4: S1.ENA, Onderdeel1.D10_PWM/SS
  N5: S1.IN1, Onderdeel1.D9_PWM
  N6: S1.IN2, Onderdeel1.D8
  N7: S1.IN3, Onderdeel1.D7
  N8: S1.IN4, Onderdeel1.D6_PWM
  N9: S1.ENB, Onderdeel1.D5_PWM
  N10: S1.M2-01, MB.pin_2
  N11: S1.M2-02, MB.pin_1

custom parts:
  H-Bridge with L298N: h-bridge
