# Fritzing sketch ServoSlot (saved by Fritzing 0.9.2b)
breadboards: 1

parts:
  Onderdeel1 = Arduino Uno (Rev3)
  LED1 = LED - 5mm [color="Red (633nm)" package="5 mm [THT]"]
  R1 = Resistor [tolerance=±5% resistance=220 package=THT]
  LED2 = LED - 5mm [color="Green (570nm)" package="5 mm [THT]"]
  R2 = Resistor [tolerance=±5% resistance=220 package=THT]
  LED3 = LED - 5mm [color="Yellow (595nm)" package="5 mm [THT]"]
  R3 = Resistor [tolerance=±5% resistance=220 package=THT]
  J1 = Basic Servo
  J2 = Piezo Speaker
  R4 = Resistor [tolerance=±5% resistance=1M package=THT]
  C1 = Electrolytic Capacitor [capacitance=10µF package="100 mil [THT, electrolytic]"]
  S1 = Pushbutton [package="[THT]"]
  R5 = Resistor [tolerance=±5% resistance=10k package=THT]

nets:
  N1: Onderdeel1.A0, J2.pin1, R4.Pin_0
  N2: Onderdeel1.D9_PWM, J1.pulse
  N3: Onderdeel1.D2, S1.Pin_1, S1.Pin_2, R5.Pin_0
  N4: Onderdeel1.D3_PWM, R3.Pin_1
  N5: Onderdeel1.D4, R2.Pin_1
  N6: Onderdeel1.D5_PWM, R1.Pin_1
  5V: Onderdeel1.5V, J1.vcc, J2.pin2, C1.+, S1.Pin_3, S1.Pin_4
  GND: Onderdeel1.GND, LED1.cathode, LED2.cathode, LED3.cathode, J1.gnd, R4.Pin_1, C1.-, R5.Pin_1
  N7: LED1.anode, R1.Pin_0
  N8: LED2.anode, R2.Pin_0
  N9: LED3.anode, R3.Pin_0
